// Logisim project KeyBuffer.circ as structural Verilog: 1 circuit, main circuit main
module main (
  input  DAV,
  input  ACK,
  output DAC,
  output Wreg,
  output [3:0] D0_3,
  output Dval
);

  wire Mclk_out;

  Clock Mclk (.out(Mclk_out));
  // ATF750c Dumb_PAL: pin names not known; wires that end beside it: Mclk_out, DAV, ACK, 1'b0, 1'b1, DAC, Wreg, D0_3[3], D0_3[2], D0_3[1], D0_3[0], Dval
endmodule
