// Logisim project KeyboardReader.circ as structural Verilog: 1 circuit, main circuit main
module main (
  input  ACK,
  output [3:0] D0_3,
  output Dval
);

  wire Clk_out, Mclk_out, n4x4_matrix_keyboard_1_p4, n4x4_matrix_keyboard_1_p5, n4x4_matrix_keyboard_1_p6,
       n4x4_matrix_keyboard_1_p7;
  wire [2:0] n4x4_matrix_keyboard_1_p1;

  // _4x4_Matrix_Keyboard 4x4_matrix_keyboard_1: pin names not known; wires that end beside it: n4x4_matrix_keyboard_1_p1[0], n4x4_matrix_keyboard_1_p1[1], n4x4_matrix_keyboard_1_p1[2], n4x4_matrix_keyboard_1_p4, n4x4_matrix_keyboard_1_p5, n4x4_matrix_keyboard_1_p6, n4x4_matrix_keyboard_1_p7
  Pull_Resistor #(.pull(1)) pull_resistor_1 (.node(n4x4_matrix_keyboard_1_p4));
  Pull_Resistor #(.pull(1)) pull_resistor_2 (.node(n4x4_matrix_keyboard_1_p5));
  Pull_Resistor #(.pull(1)) pull_resistor_3 (.node(n4x4_matrix_keyboard_1_p6));
  Pull_Resistor #(.pull(1)) pull_resistor_4 (.node(n4x4_matrix_keyboard_1_p7));
  Clock #(.highDuration(2), .lowDuration(2)) Clk (.out(Clk_out));
  Clock Mclk (.out(Mclk_out));
  // ATF750c Dumb_PAL: pin names not known; wires that end beside it: Mclk_out, Clk_out, n4x4_matrix_keyboard_1_p4, n4x4_matrix_keyboard_1_p5, n4x4_matrix_keyboard_1_p6, n4x4_matrix_keyboard_1_p7, ACK, 1'b0, 1'b1, D0_3[3], D0_3[2], D0_3[1], D0_3[0], Dval, n4x4_matrix_keyboard_1_p1[2], n4x4_matrix_keyboard_1_p1[1], n4x4_matrix_keyboard_1_p1[0]
  // UsbPort usbport_1: pin names not known
endmodule
