// Logisim project SerialReceiver.circ as structural Verilog: 1 circuit, main circuit main
module main (
  input  SCLK,
  input  SDX,
  input  nSS,
  input  accept,
  output DXval
);

  wire atf750c_1_p8, atf750c_1_p9, atf750c_1_p10, atf750c_1_p11, atf750c_1_p12, atf750c_1_p13, MClk_out;

  Clock MClk (.out(MClk_out));
  // ATF750c atf750c_1: pin names not known; wires that end beside it: SCLK, MClk_out, SDX, nSS, accept, 1'b0, 1'b1, atf750c_1_p8, atf750c_1_p9, atf750c_1_p10, atf750c_1_p11, atf750c_1_p12, atf750c_1_p13, DXval
  LED Q1 (.in(atf750c_1_p8));
  LED Q0 (.in(atf750c_1_p9));
  LED D0 (.in(atf750c_1_p10));
  LED D1 (.in(atf750c_1_p11));
  LED D2 (.in(atf750c_1_p12));
  LED D3 (.in(atf750c_1_p13));
endmodule
