// Logisim project ShiftRegister.circ as structural Verilog: 1 circuit, main circuit main
module main (
  input  SCLK,
  input  SDX,
  input  enableShift
);

  wire Shift_Register_p6, Shift_Register_p7, Shift_Register_p8, Shift_Register_p9;

  // ATF750c Shift_Register: pin names not known; wires that end beside it: SCLK, SDX, enableShift, 1'b0, 1'b1, Shift_Register_p6, Shift_Register_p7, Shift_Register_p8, Shift_Register_p9
  LED D3 (.in(Shift_Register_p6));
  LED D1 (.in(Shift_Register_p8));
  LED D0 (.in(Shift_Register_p9));
  LED D2 (.in(Shift_Register_p7));
endmodule
