// Logisim project SerialSoundController.circ as structural Verilog: 1 circuit, main circuit main
module main (
  input  SCLK,
  input  nSS,
  input  SDX,
  output [1:0] sid0__1,
  output [1:0] vol0__1,
  output Play
);

  wire MCLK_out;

  Clock MCLK (.out(MCLK_out));
  // ATF750c atf750c_1: pin names not known; wires that end beside it: SCLK, MCLK_out, nSS, SDX, 1'b0, 1'b1, Play
endmodule
