// Logisim project 2BitRegister.circ as structural Verilog: 1 circuit, main circuit main
module main (
  input  [1:0] in_1,
  input  [1:0] in_2,
  input  [1:0] in_3,
  output [1:0] out_4,
  output [1:0] out_5,
  output [1:0] out_6
);

  wire clock_1_out, clock_3_out, Old_library_p1;

  Clock clock_1 (.out(clock_1_out));
  // ATF750c New_library: pin names not known; wires that end beside it: clock_1_out, in_3[0], in_3[1], 1'b0, 1'b1
  // ATF750c Old_library: pin names not known; wires that end beside it: Old_library_p1, in_2[0], in_2[1], 1'b0, 1'b1
  Clock clock_2 (.out(Old_library_p1));
  Clock clock_3 (.out(clock_3_out));
  // ATF750c Older_library: pin names not known; wires that end beside it: clock_3_out, in_1[0], in_1[1], 1'b0, 1'b1
endmodule
