// Logisim project DeMux1x4.circ as structural Verilog: 1 circuit, main circuit main
module main (
  input  enableCmd,
  input  [1:0] in_2
);

  wire atf750c_1_p6, atf750c_1_p7, atf750c_1_p8;

  // ATF750c atf750c_1: pin names not known; wires that end beside it: enableCmd, in_2[0], in_2[1], 1'b0, 1'b1, atf750c_1_p6, atf750c_1_p7, atf750c_1_p8
  LED set_volume (.in(atf750c_1_p6));
  LED set_sound (.in(atf750c_1_p7));
  LED play (.in(atf750c_1_p8));
endmodule
