// Logisim project SoundControl.circ as structural Verilog: 1 circuit, main circuit main
module main (
  input  Dval,
  output done,
  output cmd
);

  wire clock_1_out;

  Clock clock_1 (.out(clock_1_out));
  // ATF750c atf750c_1: pin names not known; wires that end beside it: clock_1_out, Dval, 1'b0, 1'b1, done, cmd
endmodule
