// Logisim project SoundController.circ as structural Verilog: 1 circuit, main circuit main
module main (
  input  Dval,
  input  [3:0] Din0__3,
  output done,
  output [1:0] vol0__1,
  output [1:0] sid0__1
);

  wire atf750c_1_p10, clock_1_out;

  Clock clock_1 (.out(clock_1_out));
  // ATF750c atf750c_1: pin names not known; wires that end beside it: clock_1_out, Dval, 1'b0, 1'b1, done, vol0__1[1], vol0__1[0], sid0__1[1], sid0__1[0], atf750c_1_p10
  LED Play (.in(atf750c_1_p10));
endmodule
