// Logisim project space-invaders.circ as structural Verilog: 6 circuits, main circuit space-invaders
module space_invaders (
  input  M,
  output [3:0] K0_3,
  output accept,
  output [1:0] sid0_1,
  output [1:0] vol0_1
);

  wire ACK, Dval, E, MCLK_2_out, Mclk_3_out, nLCD_sel, nSSC_sel, RS, ScanClk_out, SCLK, SDX, SLCDC_p7,
       SSC_p8, usbport_1_p8;
  wire [2:0] KBD_in0_2;
  wire [3:0] D4_7, KBD_out0_3;

  // LCD_16x2 lcd_16x2_1: pin names not known
  // ISEL_LIC_UsbPort usbport_1: pin names not known; wires that end beside it: accept, ACK, nSSC_sel, nLCD_sel, SCLK, SDX, M, usbport_1_p8
  // _4x4_Matrix_Keyboard 4x4_matrix_keyboard_1: pin names not known; wires that end beside it: D4_7[3], D4_7[2], D4_7[1], D4_7[0], KBD_in0_2[0], KBD_in0_2[1], KBD_in0_2[2], KBD_out0_3[0], KBD_out0_3[1], KBD_out0_3[2], KBD_out0_3[3], E, 1'b0, RS, 1'b0
  Button Coin (.out(usbport_1_p8));
  Pull_Resistor #(.pull(1)) pull_resistor_1 (.node(KBD_out0_3[0]));
  Pull_Resistor #(.pull(1)) pull_resistor_2 (.node(KBD_out0_3[1]));
  Pull_Resistor #(.pull(1)) pull_resistor_3 (.node(KBD_out0_3[2]));
  Pull_Resistor #(.pull(1)) pull_resistor_4 (.node(KBD_out0_3[3]));
  // ATF750c SLCDC: pin names not known; wires that end beside it: K0_3[2], K0_3[1], K0_3[0], SCLK, SDX, nLCD_sel, SLCDC_p7, 1'b0, 1'b1, E, RS
  Clock MCLK (.out(SLCDC_p7));
  Clock MCLK_2 (.out(MCLK_2_out));
  Clock #(.highDuration(2), .lowDuration(2)) ScanClk (.out(ScanClk_out));
  // ATF750c SSC: pin names not known; wires that end beside it: 1'b0, SCLK, MCLK_2_out, nSSC_sel, SDX, 1'b0, 1'b1, SSC_p8
  Clock Mclk_3 (.out(Mclk_3_out));
  // ATF750c Keyboard_Reader: pin names not known; wires that end beside it: Mclk_3_out, ScanClk_out, ACK, 1'b0, 1'b1, K0_3[3], K0_3[2], K0_3[1], K0_3[0], Dval, KBD_in0_2[2], KBD_in0_2[1], KBD_in0_2[0]
  LED Play (.in(SSC_p8));
endmodule

module UsbPort (
  input  Coin,
  input  M,
  output accept
);

  wire ACK, SCLK, SDX, srl_SS, srs_SS;

  // ISEL_LIC_UsbPort usbport_1: pin names not known; wires that end beside it: accept, ACK, srs_SS, srl_SS, SCLK, SDX, M, Coin
endmodule

module Keyboard (
);

  wire [2:0] KBD_in0_2;
  wire [3:0] KBD_out0_3;

  // _4x4_Matrix_Keyboard 4x4_matrix_keyboard_1: pin names not known; wires that end beside it: KBD_in0_2[0], KBD_in0_2[1], KBD_in0_2[2], KBD_out0_3[0], KBD_out0_3[1], KBD_out0_3[2], KBD_out0_3[3]
  Pull_Resistor #(.pull(1)) pull_resistor_1 (.node(KBD_out0_3[0]));
  Pull_Resistor #(.pull(1)) pull_resistor_2 (.node(KBD_out0_3[3]));
  Pull_Resistor #(.pull(1)) pull_resistor_3 (.node(KBD_out0_3[1]));
  Pull_Resistor #(.pull(1)) pull_resistor_4 (.node(KBD_out0_3[2]));
endmodule

module Keyboard_Reader (
  output [3:0] D0_3
);

  wire ACK, atf750c_1_p1, Clk_out, Dval;
  wire [2:0] KBD_in0_2;
  wire [3:0] KBD_out0_3;

  Clock #(.highDuration(2), .lowDuration(2)) Clk (.out(Clk_out));
  // ATF750c atf750c_1: pin names not known; wires that end beside it: atf750c_1_p1, Clk_out, KBD_out0_3[0], KBD_out0_3[1], KBD_out0_3[2], KBD_out0_3[3], ACK, 1'b0, 1'b1, D0_3[3], D0_3[2], D0_3[1], D0_3[0], Dval, KBD_in0_2[2], KBD_in0_2[1], KBD_in0_2[0]
  Clock Mclk (.out(atf750c_1_p1));
endmodule

module LCD (
);

  wire [3:0] D4_7;

  // LCD_16x2 lcd_16x2_1: pin names not known; wires that end beside it: D4_7[3], D4_7[2], D4_7[1], D4_7[0]
endmodule

module Serial_LCD_Controller (
);

  wire atf750c_1_p14, atf750c_1_p15, Dispatcher_Clock_out, E, RS, SCLK, SDX, SRClk_out, srl_SS;
  wire [3:0] D4_7;

  Clock Dispatcher_Clock (.out(Dispatcher_Clock_out));
  Clock SRClk (.out(SRClk_out));
  // ATF750c atf750c_1: pin names not known; wires that end beside it: SCLK, SDX, srl_SS, Dispatcher_Clock_out, SRClk_out, 1'b0, 1'b1, E, RS, D4_7[0], D4_7[1], D4_7[2], D4_7[3], atf750c_1_p14, atf750c_1_p15
  LED E1 (.in(atf750c_1_p14));
  LED E0 (.in(atf750c_1_p15));
endmodule
