// Logisim project KBDTest.circ as structural Verilog: 1 circuit, main circuit KBDTest
module KBDTest (
  output [3:0] K0_3
);

  wire ACK, Dval, KeyboardReader_p5, ScanCLK_out;
  wire [2:0] KBD_in0_2;
  wire [3:0] KBD_out0_3;

  // _4x4_Matrix_Keyboard Keyboard: pin names not known; wires that end beside it: KBD_in0_2[0], KBD_in0_2[1], KBD_in0_2[2], KBD_out0_3[0], KBD_out0_3[1], KBD_out0_3[2], KBD_out0_3[3]
  // UsbPort usbport_1: pin names not known; wires that end beside it: ACK
  Pull_Resistor #(.pull(1)) pull_resistor_1 (.node(KBD_out0_3[0]));
  Pull_Resistor #(.pull(1)) pull_resistor_2 (.node(KBD_out0_3[1]));
  Pull_Resistor #(.pull(1)) pull_resistor_3 (.node(KBD_out0_3[2]));
  Pull_Resistor #(.pull(1)) pull_resistor_4 (.node(KBD_out0_3[3]));
  Clock #(.highDuration(2), .lowDuration(2)) ScanCLK (.out(ScanCLK_out));
  // ATF750c KeyboardReader: pin names not known; wires that end beside it: K0_3[3], K0_3[2], K0_3[1], K0_3[0], KeyboardReader_p5, ScanCLK_out, KBD_out0_3[0], KBD_out0_3[1], KBD_out0_3[2], KBD_out0_3[3], ACK, 1'b0, 1'b1, K0_3[3], K0_3[2], K0_3[1], K0_3[0], Dval, KBD_in0_2[2], KBD_in0_2[1], KBD_in0_2[0]
  Clock MCLK (.out(KeyboardReader_p5));
endmodule
