// Logisim project SoundGeneratorTest.circ as structural Verilog: 1 circuit, main circuit SoundGeneratorTest
module SoundGeneratorTest (
  output [1:0] sid0_1,
  output [1:0] vol0_1,
  output Play
);

  wire nSSC_sel, SCLK, SDX, SSC_p2;

  // UsbPort usbport_1: pin names not known; wires that end beside it: nSSC_sel, SCLK, SDX
  // ATF750c SSC: pin names not known; wires that end beside it: SCLK, SSC_p2, nSSC_sel, SDX, 1'b0, 1'b1, sid0_1[1], sid0_1[0], vol0_1[1], vol0_1[0], Play
  Clock MCLK (.out(SSC_p2));
endmodule
