// Logisim project SerialLCDController.circ as structural Verilog: 1 circuit, main circuit main
module main (
  input  SCLK,
  input  SDX,
  input  nSS
);

  wire clock_1_out, SLCDC_p5, SLCDC_p8, SLCDC_p9, SLCDC_p10, SLCDC_p11, SLCDC_p12, SLCDC_p13, SLCDC_p14,
       SLCDC_p15;

  Clock clock_1 (.out(clock_1_out));
  // ATF750c SLCDC: pin names not known; wires that end beside it: SCLK, SDX, nSS, clock_1_out, SLCDC_p5, 1'b0, 1'b1, SLCDC_p8, SLCDC_p9, SLCDC_p10, SLCDC_p11, SLCDC_p12, SLCDC_p13, SLCDC_p14, SLCDC_p15
  Clock clock_2 (.out(SLCDC_p5));
  // LCD_16x2 lcd_16x2_1: pin names not known; wires that end beside it: SLCDC_p13, SLCDC_p12, SLCDC_p11, SLCDC_p10
  LED E0 (.in(SLCDC_p15));
  LED E1 (.in(SLCDC_p14));
endmodule
