// Logisim project 3BitCounter.circ as structural Verilog: 1 circuit, main circuit main
module main (
  input  clr
);

  wire _3BitCounter_p5, _3BitCounter_p6, SCLK_out;

  Clock SCLK (.out(SCLK_out));
  // ATF750c _3BitCounter: pin names not known; wires that end beside it: SCLK_out, clr, 1'b0, 1'b1, _3BitCounter_p5, _3BitCounter_p6
  LED pFlag (.in(_3BitCounter_p5));
  LED dFlag (.in(_3BitCounter_p6));
endmodule
