// Logisim project ParityCheck.circ as structural Verilog: 1 circuit, main circuit main
module main (
  input  SCLK,
  input  SDX,
  input  init
);

  wire Parity_Check_p6;

  // ATF750c Parity_Check: pin names not known; wires that end beside it: SCLK, SDX, init, 1'b0, 1'b1, Parity_Check_p6
  LED err (.in(Parity_Check_p6));
endmodule
