// Logisim project SerialControl.circ as structural Verilog: 1 circuit, main circuit main
module main (
  input  MClk,
  input  SS,
  input  accept,
  input  pFlag,
  input  dFlag,
  input  RXerror
);

  wire Serial_Control_p9, Serial_Control_p10, Serial_Control_p11;

  // ATF750c Serial_Control: pin names not known; wires that end beside it: MClk, SS, accept, pFlag, dFlag, RXerror, 1'b0, 1'b1, Serial_Control_p9, Serial_Control_p10, Serial_Control_p11
  LED DXval (.in(Serial_Control_p9));
  LED init (.in(Serial_Control_p10));
  LED wr (.in(Serial_Control_p11));
endmodule
