// Logisim project COINTest.circ as structural Verilog: 1 circuit, main circuit COINTest
module COINTest (
  output accept
);

  wire usbport_1_p2;

  // UsbPort usbport_1: pin names not known; wires that end beside it: accept, usbport_1_p2
  Button Coin (.out(usbport_1_p2));
endmodule
