// Logisim project HALTest.circ as structural Verilog: 1 circuit, main circuit HALTest
module HALTest (
  input  in_1,
  input  in_2,
  input  in_3,
  input  in_4,
  input  in_5,
  input  in_6,
  input  in_7,
  input  in_8,
  output out_9,
  output out_10,
  output out_11,
  output out_12,
  output out_13,
  output out_14,
  output out_15,
  output out_16
);

  // UsbPort usbport_1: pin names not known; wires that end beside it: out_9, out_10, out_11, out_12, out_13, out_14, out_15, out_16, in_1, in_2, in_3
endmodule
