// Logisim project LCDTest.circ as structural Verilog: 1 circuit, main circuit Serial LCD Controller
module Serial_LCD_Controller (
);

  wire E, MCLK_out, nLCD_sel, RS, SCLK, SDX;
  wire [3:0] D4_7;

  // LCD_16x2 LCD: pin names not known; wires that end beside it: D4_7[3], D4_7[2], D4_7[1], D4_7[0]
  // UsbPort usbport_1: pin names not known; wires that end beside it: nLCD_sel, SCLK, SDX
  Clock MCLK (.out(MCLK_out));
  // ATF750c SLCDC: pin names not known; wires that end beside it: SCLK, SDX, nLCD_sel, MCLK_out, 1'b0, 1'b1, E, RS
endmodule
